// Digital circuit Counter.dig as structural Verilog
module Counter (
  input  CLK,
  input  RESET,
  output [3:0] OUT,
  output TC
);

  wire or_1_out;
  wire [3:0] add_1_s, multiplexer_1_out;

  Add #(.Bits(4)) add_1 (.a(OUT), .b(4'b0001), .c_i(1'b0), .s(add_1_s));  // open: c_o
  Comparator #(.Bits(4)) comparator_1 (.a(OUT), .b(4'b1001), .eq(TC));  // open: gt, lt
  Multiplexer #(.Bits(4)) multiplexer_1 (.sel(or_1_out), .in_0(add_1_s), .in_1(4'b0000), .out(multiplexer_1_out));
  or or_1 (or_1_out, TC, RESET);
  D_FF #(.Bits(4), .Default(11)) d_ff_1 (.D(multiplexer_1_out), .C(CLK), .Q(OUT));  // open: nQ

  // Notes on the sheet:
  //   CLK: Hz: 2
endmodule

/* Test case Static:
CLK RESET OUT TC

C   1     0   0
loop(n,20)
let out = (n+1)%10;
C   0     (out) (out=9)
end loop
*/

/* Test case Dynamic:
CLK RESET OUT TC

0   0     X   X
while(OUT !=0)
C   0     X   X
end while

0   0     0   0
repeat(20) C   0     ((OUT+1)%10) (OUT=8)
*/

/* Test case Failing:
CLK RESET OUT TC

C   1     0   0
C   0     1   0
loop(n,4)
C   0     4   (n=1)
end loop
*/
